# Fritzing sketch gps_tracker (saved by Fritzing 0.9.5d)
circuit board: 10.2138cm x 7.39158cm

parts:
  U1 = ESP8266 NodeMCU LoLin module
  A1 = u-blox NEO-6M GPS Breakout
  buz1 = Piezo Buzzer

nets:
  N1: U1.D0, buz1.pin_1
  N2: U1.D1, A1.Pin_4
  N3: U1.D2, A1.Pin_3
  N4: U1.3V3, A1.Pin_1
  N5: U1.GND, A1.Pin_2, buz1.pin_2

custom parts:
  ESP8266 NodeMCU LoLin module: ESP8266 based NodeMCU
  Piezo Buzzer: Part from https://www.nutsvolts.com/magazine/article/november2012_SmileysWorkshop. Breadboard and icon images modified to be 0.3" in spacing and be more similar to the actual physical part.
